# Fritzing sketch bee-weighter (saved by Fritzing 0.9.4)

parts:
  Part6 = Arduino Pro Mini (3.3V)
  ZS-042_RTC1 = ZS-042 RTC Module
  Part7 = HX711 Weighing Sensor Module

nets:
  5V: Part6.VCC, ZS-042_RTC1.VCC, Part7.VCC
  GND: Part6.GND, ZS-042_RTC1.GND, Part7.GND
  N1: Part6.A3, Part7.CK/TX
  N2: Part6.A2, Part7.DO/RX
  N3: Part6.D5, ZS-042_RTC1.32K
  N4: Part6.D4, ZS-042_RTC1.SQW
  N5: Part6.D3, ZS-042_RTC1.SCL
  N6: Part6.D2, ZS-042_RTC1.SDA
