# Fritzing sketch 1-strain (saved by Fritzing 0.9.4)

parts:
  Part6 = Arduino Pro Mini (3.3V)
  ZS-042_RTC1 = ZS-042 RTC Module
  Part7 = HX711 Weighing Sensor Module
  R2 = Resistor [tolerance=±5% resistance=1k package=THT]
  J1 = Camdenboss CTB0158-3 [part_number=CTB0158-3 package=THT]
  R1 = Resistor [tolerance=±5% resistance=1k package=THT]

nets:
  5V: Part6.VCC, ZS-042_RTC1.VCC, Part7.VCC
  GND: Part6.GND, ZS-042_RTC1.GND, Part7.GND
  N1: Part6.A3, Part7.CK/TX
  N2: Part6.A2, Part7.DO/RX
  N3: Part6.D5, ZS-042_RTC1.32K
  N4: Part6.D4, ZS-042_RTC1.SQW
  N5: Part6.D3, ZS-042_RTC1.SCL
  N6: Part6.D2, ZS-042_RTC1.SDA
  N7: Part7.E+, J1.pin3
  N8: Part7.E-, R2.Pin_1, J1.pin2
  N9: Part7.A+, R2.Pin_0, R1.Pin_0
  N10: Part7.A-, J1.pin1, R1.Pin_1
  RED: J1.terminal_1
  BLACK: J1.terminal_2
  WHITE: J1.terminal_3
