# Fritzing sketch 2-strain (saved by Fritzing 0.9.4)

parts:
  Part6 = Arduino Pro Mini (3.3V)
  ZS-042_RTC1 = ZS-042 RTC Module
  J1 = Camdenboss CTB0158-3 [part_number=CTB0158-3 package=THT]
  Part7 = HX711 Weighing Sensor Module
  J2 = Camdenboss CTB0158-3 [part_number=CTB0158-3 package=THT]

nets:
  5V: Part6.VCC, ZS-042_RTC1.VCC, Part7.VCC
  GND: Part6.GND, ZS-042_RTC1.GND, Part7.GND
  N1: Part6.A3, Part7.CK/TX
  N2: Part6.A2, Part7.DO/RX
  N3: Part6.D5, ZS-042_RTC1.32K
  N4: Part6.D4, ZS-042_RTC1.SQW
  N5: Part6.D3, ZS-042_RTC1.SCL
  N6: Part6.D2, ZS-042_RTC1.SDA
  N7: J1.pin1, Part7.A-
  N8: J1.pin2, Part7.E-, J2.pin3
  N9: J1.pin3, Part7.E+, J2.pin2
  N10: Part7.A+, J2.pin1
