# Fritzing sketch 4-strain (saved by Fritzing 0.9.4)

parts:
  ZS-042_RTC1 = ZS-042 RTC Module
  Part7 = HX711 Weighing Sensor Module
  J2 = Camdenboss CTB0158-3 [part_number="Upper right" package=THT]
  J3 = Camdenboss CTB0158-3 [part_number="Upper left" package=THT]
  J4 = Camdenboss CTB0158-3 [part_number="Lower right" package=THT]
  Part6 = Arduino Pro Mini (3.3V)
  J1 = Camdenboss CTB0158-3 [part_number="Lower left" package=THT]

nets:
  GND: ZS-042_RTC1.GND, Part7.GND, Part6.GND
  5V: ZS-042_RTC1.VCC, Part7.VCC, Part6.VCC
  N1: ZS-042_RTC1.SDA, Part6.D2
  N2: ZS-042_RTC1.SCL, Part6.D3
  N3: ZS-042_RTC1.SQW, Part6.D4
  N4: ZS-042_RTC1.32K, Part6.D5
  N5: Part7.DO/RX, Part6.A2
  N6: Part7.CK/TX, Part6.A3
  N7: Part7.E+, J4.pin1
  N8: Part7.E-, J3.pin1
  N9: Part7.A+, J2.pin1
  N10: Part7.A-, J1.pin1
  N11: J2.pin2, J4.pin2
  N12: J2.pin3, J3.pin3
  N13: J3.pin2, J1.pin2
  N14: J4.pin3, J1.pin3
